# Fritzing sketch button_part (saved by Fritzing 1.0.2b)
breadboards: 1

parts:
  Part1 = Arduino Uno (Rev3)
  R1 = Resistor [tolerance=±5% power=0.25W resistance=1000 package=THT]
  S1 = Round Pushbutton

nets:
  N1: Part1.D2, R1.Pin_1, S1.leg0
  N2: Part1.5V, S1.leg1
  N3: Part1.GND, R1.Pin_0

notes:
  1k resistor
