# Fritzing sketch combined (saved by Fritzing 1.0.2b)
breadboards: 1

parts:
  Part1 = Arduino Uno (Rev3)
  DFRobot_DFPlayer_Mini1 = DFRobot DFPlayer Mini [part_number=DFR0299]
  SP1 = SPEAKER [package=pcb_mount_speaker]
  R1 = Resistor [tolerance=±5% power=0.25W resistance=220 package=THT]
  S2 = Round Pushbutton
  R2 = Resistor [tolerance=±5% power=0.25W resistance=220 package=THT]

nets:
  N1: Part1.D10_PWM/SS, DFRobot_DFPlayer_Mini1.IO_2
  N2: Part1.GND, DFRobot_DFPlayer_Mini1.RX, DFRobot_DFPlayer_Mini1.USB_NEG, R2.Pin_1
  N3: Part1.D2, S2.leg0, R2.Pin_0
  N4: Part1.5V, DFRobot_DFPlayer_Mini1.IO_1, S2.leg1
  N5: DFRobot_DFPlayer_Mini1.GND-1, DFRobot_DFPlayer_Mini1.GND-2, R1.Pin_0
  N6: DFRobot_DFPlayer_Mini1.USB_POS, SP1.+
  N7: DFRobot_DFPlayer_Mini1.BUSY, SP1.-

notes:
  1k resistor
